# Fritzing sketch teensy_bob_2 (saved by Fritzing 0.9.1b)
circuit board: 5.08cm x 5.08cm
breadboards: 1

parts:
  Teensy_3_1 = Teensy 3.1
  I2C = female pin header, 4 pins [form="♀ (female)"]
  M1 = female pin header, 3 pins [form="♀ (female)"]
  M2 = female pin header, 3 pins [form="♀ (female)"]
  M3 = female pin header, 3 pins [form="♀ (female)"]
  M4 = female pin header, 3 pins [form="♀ (female)"]
  USB_PWR = USB Connectors [package=usb-a-s-nosilk]
  PI = female pin header, 3 pins [form="♀ (female)"]
  SONAR = female pin header, 3 pins [form="♀ (female)"]
  OFS = female pin header, 6 pins [form="♀ (female)"]
  V2 = female pin header, 1 pin [form="♀ (female)"]

nets:
  GND: Teensy_3_1.GND, I2C.pin4, M1.pin3, M2.pin3, M3.pin3, M4.pin3, USB_PWR.GND, PI.pin1, SONAR.pin1, OFS.pin1
  N1: Teensy_3_1.D0, PI.pin2
  N2: Teensy_3_1.D1, PI.pin3
  N3: Teensy_3_1.D7, SONAR.pin3
  N4: Teensy_3_1.D10, OFS.pin3
  N5: Teensy_3_1.D11, OFS.pin5
  N6: Teensy_3_1.D12, OFS.pin4
  N7: Teensy_3_1.D13, OFS.pin6
  N8: Teensy_3_1.A4/D18, I2C.pin3
  N9: Teensy_3_1.A5/D19, I2C.pin2
  N10: Teensy_3_1.A6/D20, M4.pin1
  N11: Teensy_3_1.A7/D21, M3.pin1
  N12: Teensy_3_1.A8/D22, M2.pin1
  N13: Teensy_3_1.A9/D23, M1.pin1
  N14: Teensy_3_1.3V3, I2C.pin1
  N15: Teensy_3_1.Vin, M2.pin2
  N16: M1.pin2, V2.pin1
  N17: M3.pin2, SONAR.pin2, OFS.pin2
  N18: M4.pin2, USB_PWR.VBUS

notes:
  D + -
  - + CS MISO MOSI CLK
  - + RX
  - RX TX
  + SCL SDA -
  Kevin Sheridan
