# Fritzing sketch teensy_breakout_1 (saved by Fritzing 0.9.1b)
circuit board: 7.62cm x 7.62cm
breadboards: 1

parts:
  Teensy_3_1 = Teensy 3.1
  M1 = female pin header, 3 pins [form="♀ (female)"]
  M2 = female pin header, 3 pins [form="♀ (female)"]
  M3 = female pin header, 3 pins [form="♀ (female)"]
  M4 = female pin header, 3 pins [form="♀ (female)"]
  Pi = female pin header, 3 pins [form="♀ (female)"]
  I2C = female pin header, 4 pins [form="♀ (female)"]
  Sonar = female pin header, 3 pins [form="♀ (female)"]
  OFS = female pin header, 6 pins [form="♀ (female)"]
  USB_PWR = USB Connectors [part_number=09011 package=usb-a-s-nosilk]

nets:
  GND: Teensy_3_1.GND, M1.pin3, M2.pin3, M3.pin3, M4.pin3, Pi.pin3, I2C.pin1, Sonar.pin3, OFS.pin1, USB_PWR.GND
  N1: Teensy_3_1.D0, Pi.pin2
  N2: Teensy_3_1.D1, Pi.pin1
  N3: Teensy_3_1.D7, Sonar.pin1
  N4: Teensy_3_1.D10, OFS.pin3
  N5: Teensy_3_1.D11, OFS.pin5
  N6: Teensy_3_1.D12, OFS.pin4
  N7: Teensy_3_1.D13, OFS.pin6
  N8: Teensy_3_1.A4/D18, I2C.pin2
  N9: Teensy_3_1.A5/D19, I2C.pin3
  N10: Teensy_3_1.A6/D20, M4.pin1
  N11: Teensy_3_1.A7/D21, M3.pin1
  N12: Teensy_3_1.A8/D22, M2.pin1
  N13: Teensy_3_1.A9/D23, M1.pin1
  N14: Teensy_3_1.3V3, I2C.pin4
  N15: Teensy_3_1.Vin, M1.pin2
  N16: M2.pin2, Sonar.pin2, OFS.pin2
  N17: M3.pin2, USB_PWR.VBUS

notes:
  D + -
  - RX TX
  - D C +
  RX + -
  - + CS MISO MOSI CLK

// code stored in the sketch: teensy_breakout_1.ino

