# Fritzing sketch Quadcopter_schem (saved by Fritzing 0.8.7b)
circuit board: 8.46667cm x 5.64444cm
breadboards: 1

parts:
  Part1 = Arduino Mega 2560 (Rev3)
  Part2 = 9 Degrees of Freedom - Sensor Stick
  U1 = MPL3115A2 [package=lga8]
  U2 = LIPO-2000mAh [package=lipo-2000]
  U3 = SUP500F [package=sup500f]
  J1 = Infrared Proximity Sensor
  J2 = Infrared Proximity Sensor
  J3 = Infrared Proximity Sensor
  J4 = Infrared Proximity Sensor
  J5 = Infrared Proximity Sensor
  J6 = Infrared Proximity Sensor
  Part3 = XBee Explorer Regulated
  U4 = XBEE-1 [package=xbee-1]  # not connected

nets:
  N1: Part1.A0, J6.Vout
  N2: Part1.A1, J3.Vout
  N3: Part1.A2, J4.Vout
  N4: Part1.A3, J2.Vout
  N5: Part1.A4, J5.Vout
  N6: Part1.A5, J1.Vout
  N7: Part1.D20/SDA, Part1.SDA, Part2.SDA, U1.SDA
  N8: Part1.D17_PWM/RX2, Part3.DOUT
  N9: Part1.D16_PWM/TX2, Part3.DIN
  N10: Part1.D15/RX3, U3.RX-I
  N11: Part1.D14/TX3, U3.TX-O
  GND: Part1.GND, Part2.GND, U1.GND, U2.-, U3.GND, J1.GND, J2.GND, J3.GND, J4.GND, J5.GND, J6.GND, Part3.GND
  N12: Part2.SCL, U1.SCL
  VCC: Part2.VCC, U1.VDD, U2.+, U3.VCC, J1.Vcc, J2.Vcc, J3.Vcc, J4.Vcc, J5.Vcc, J6.Vcc, Part3.5V

notes:
  5 Volts at 8 amps from ESC(4 each @ 5 Volts and 2 amps)
  I2C barometer
  9 DOF IMU (I2C)
  GPS (Tx & Rx)
  IR distance Sensors
