# Fritzing sketch Teensy_breakout (saved by Fritzing 0.9.0b)
circuit board: 8.46667cm x 5.64444cm
perfboards: 1

parts:
  Teensy_3_1 = Teensy 3.1
  JP1 = Header 1 [package=1x01_offset]  # not connected
  JP2 = Header 1 [package=1x01_offset]  # not connected
  JP3 = Header 1 [package=1x01_offset]
  JP4 = Header 1 [package=1x01_offset]
  JP5 = Header 1 [package=1x01_offset]
  JP6 = Header 1 [package=1x01_offset]
  JP7 = Header 1 [package=1x01_offset]  # not connected
  JP8 = Header 1 [package=1x01_offset]  # not connected
  JP9 = Header 1 [package=1x01_offset]  # not connected
  JP10 = Header 1 [package=1x01_offset]
  JP11 = Header 1 [package=1x01_offset]
  JP12 = Header 1 [package=1x01_offset]
  JP13 = Header 1 [package=1x01_offset]
  JP14 = Header 1 [package=1x01_offset]  # not connected
  JP15 = Header 1 [package=1x01_offset]
  JP16 = Header 1 [package=1x01_offset]  # not connected
  JP17 = Header 1 [package=1x01_offset]
  JP18 = Header 1 [package=1x01_offset]
  JP19 = Header 1 [package=1x01_offset]  # not connected
  JP20 = Header 1 [package=1x01_offset]
  S1 = Toggle Switch [package=THT]
  JP21 = Header 1 [package=1x01_offset]
  JP22 = Header 1 [package=1x01_offset]
  JP23 = Header 1 [package=1x01_offset]
  JP24 = Header 1 [package=1x01_offset]  # not connected
  JP25 = Header 1 [package=1x01_offset]
  JP26 = Header 1 [package=1x01_offset]
  JP27 = Header 1 [package=1x01_offset]  # not connected
  JP28 = Header 1 [package=1x01_offset]  # not connected
  JP29 = Header 1 [package=1x01_offset]
  JP30 = Header 1 [package=1x01_offset]  # not connected
  JP31 = Header 1 [package=1x01_offset]
  JP32 = Header 1 [package=1x01_offset]
  JP33 = Header 1 [package=1x01_offset]
  JP34 = Header 1 [package=1x01_offset]

nets:
  N1: Teensy_3_1.GND, JP3.1, JP17.1
  N2: Teensy_3_1.D0, JP21.1
  N3: Teensy_3_1.D1, JP22.1
  N4: Teensy_3_1.D7, JP25.1
  N5: Teensy_3_1.D8, JP26.1
  N6: Teensy_3_1.D10, JP33.1
  N7: Teensy_3_1.D11, JP34.1
  N8: Teensy_3_1.D12, JP31.1
  N9: Teensy_3_1.D13, JP32.1
  N10: Teensy_3_1.A4/D18, JP6.1
  N11: Teensy_3_1.A5/D19, JP5.1
  N12: Teensy_3_1.A6/D20, JP10.1
  N13: Teensy_3_1.A7/D21, JP13.1
  N14: Teensy_3_1.A8/D22, JP15.1
  N15: Teensy_3_1.A9/D23, JP18.1
  N16: Teensy_3_1.3V3, JP4.1
  N17: Teensy_3_1.Vin, S1.L2
  N18: JP11.1, JP23.1
  N19: JP12.1, JP29.1
  N20: JP20.1, S1.COM

notes:
  I2c
  M1
  M2
  M3
  M4
  +     -
  SCK - DIN - DOUT - CS
